// Logisim project tests.circ as structural Verilog
module Test_7400 (
);

  wire and_1_out, clock_1_out, nand_1_out, undriven, undriven_2, undriven_3, undriven_4, xnor_1_out,
       xnor_2_out, xnor_3_out, xnor_4_out;
  wire [1:0] counter_1_q;

  Clock clock_1 (.out(clock_1_out));
  Counter #(.width(2), .max('h3)) counter_1 (
    .count(1'b1), .Q(counter_1_q), .clk(clock_1_out));  // open: load, D, carry, clr
  nand nand_1 (nand_1_out, counter_1_q[0], counter_1_q[1]);
  xnor xnor_1 (xnor_1_out, nand_1_out, undriven_3);
  xnor xnor_2 (xnor_2_out, nand_1_out, undriven_4);
  xnor xnor_3 (xnor_3_out, nand_1_out, undriven_2);
  xnor xnor_4 (xnor_4_out, nand_1_out, undriven);
  and and_1 (and_1_out, xnor_1_out, xnor_2_out, xnor_3_out, xnor_4_out);
  LED led_1 (.in(and_1_out));
endmodule

module Test_7402 (
);

  wire and_1_out, clock_1_out, dip_7402_1_q1, dip_7402_1_q2, dip_7402_1_q3, dip_7402_1_q4, nor_1_out,
       xnor_1_out, xnor_2_out, xnor_3_out, xnor_4_out;
  wire [1:0] counter_1_q;

  Clock clock_1 (.out(clock_1_out));
  Counter #(.width(2), .max('h3)) counter_1 (
    .count(1'b1), .Q(counter_1_q), .clk(clock_1_out));  // open: load, D, carry, clr
  DIP_7402 dip_7402_1 (
    .A1(counter_1_q[0]), .B1(counter_1_q[1]), .A2(counter_1_q[0]), .B2(counter_1_q[1]), .A3(counter_1_q[0]),
    .B3(counter_1_q[1]), .A4(counter_1_q[0]), .B4(counter_1_q[1]), .Q1(dip_7402_1_q1), .Q2(dip_7402_1_q2),
    .Q3(dip_7402_1_q3), .Q4(dip_7402_1_q4));
  nor nor_1 (nor_1_out, counter_1_q[0], counter_1_q[1]);
  xnor xnor_1 (xnor_1_out, nor_1_out, dip_7402_1_q4);
  xnor xnor_2 (xnor_2_out, nor_1_out, dip_7402_1_q3);
  xnor xnor_3 (xnor_3_out, nor_1_out, dip_7402_1_q1);
  xnor xnor_4 (xnor_4_out, nor_1_out, dip_7402_1_q2);
  and and_1 (and_1_out, xnor_1_out, xnor_2_out, xnor_3_out, xnor_4_out);
  LED led_1 (.in(and_1_out));
endmodule

module Test_7404 (
);

  wire and_1_out, clock_1_out, counter_1_q, dip_7404_1_q1, dip_7404_1_q2, dip_7404_1_q3, dip_7404_1_q4,
       dip_7404_1_q5, dip_7404_1_q6, not_1_out, xnor_1_out, xnor_2_out, xnor_3_out, xnor_4_out, xnor_5_out,
       xnor_6_out;

  Counter #(.width(1), .max('h1)) counter_1 (
    .count(1'b1), .Q(counter_1_q), .clk(clock_1_out));  // open: load, D, carry, clr
  Clock clock_1 (.out(clock_1_out));
  DIP_7404 dip_7404_1 (
    .A1(counter_1_q), .A2(counter_1_q), .A3(counter_1_q), .A4(counter_1_q), .A5(counter_1_q),
    .A6(counter_1_q), .Q1(dip_7404_1_q1), .Q2(dip_7404_1_q2), .Q3(dip_7404_1_q3), .Q4(dip_7404_1_q4),
    .Q5(dip_7404_1_q5), .Q6(dip_7404_1_q6));
  not not_1 (not_1_out, counter_1_q);
  xnor xnor_1 (xnor_1_out, not_1_out, dip_7404_1_q6);
  xnor xnor_2 (xnor_2_out, not_1_out, dip_7404_1_q5);
  xnor xnor_3 (xnor_3_out, not_1_out, dip_7404_1_q4);
  xnor xnor_4 (xnor_4_out, not_1_out, dip_7404_1_q1);
  xnor xnor_5 (xnor_5_out, not_1_out, dip_7404_1_q2);
  xnor xnor_6 (xnor_6_out, not_1_out, dip_7404_1_q3);
  LED led_1 (.in(and_1_out));
  and and_1 (and_1_out, xnor_1_out, xnor_2_out, xnor_3_out, xnor_4_out, xnor_5_out, xnor_6_out);
endmodule

module Test_7408 (
);

  wire and_1_out, and_2_out, clock_1_out, dip_7408_1_q1, dip_7408_1_q2, dip_7408_1_q3, dip_7408_1_q4,
       xnor_1_out, xnor_2_out, xnor_3_out, xnor_4_out;
  wire [1:0] counter_1_q;

  Clock clock_1 (.out(clock_1_out));
  Counter #(.width(2), .max('h3)) counter_1 (
    .count(1'b1), .Q(counter_1_q), .clk(clock_1_out));  // open: load, D, carry, clr
  DIP_7408 dip_7408_1 (
    .A1(counter_1_q[0]), .B1(counter_1_q[1]), .A2(counter_1_q[0]), .B2(counter_1_q[1]), .A3(counter_1_q[0]),
    .B3(counter_1_q[1]), .A4(counter_1_q[0]), .B4(counter_1_q[1]), .Q1(dip_7408_1_q1), .Q2(dip_7408_1_q2),
    .Q3(dip_7408_1_q3), .Q4(dip_7408_1_q4));
  and and_1 (and_1_out, counter_1_q[0], counter_1_q[1]);
  xnor xnor_1 (xnor_1_out, and_1_out, dip_7408_1_q3);
  xnor xnor_2 (xnor_2_out, and_1_out, dip_7408_1_q4);
  xnor xnor_3 (xnor_3_out, and_1_out, dip_7408_1_q1);
  xnor xnor_4 (xnor_4_out, and_1_out, dip_7408_1_q2);
  LED led_1 (.in(and_2_out));
  and and_2 (and_2_out, xnor_1_out, xnor_2_out, xnor_3_out, xnor_4_out);
endmodule

module Test_7410 (
);

  wire and_1_out, clock_1_out, dip_7410_1_q1, dip_7410_1_q2, dip_7410_1_q3, nand_1_out, xnor_1_out,
       xnor_2_out, xnor_3_out;
  wire [2:0] counter_1_q;

  Clock clock_1 (.out(clock_1_out));
  Counter #(.width(3), .max('h7)) counter_1 (
    .count(1'b1), .Q(counter_1_q), .clk(clock_1_out));  // open: load, D, carry, clr
  DIP_7410 dip_7410_1 (
    .A1(counter_1_q[0]), .B1(counter_1_q[1]), .C1(counter_1_q[2]), .A2(counter_1_q[0]), .B2(counter_1_q[1]),
    .C2(counter_1_q[2]), .A3(counter_1_q[0]), .B3(counter_1_q[1]), .C3(counter_1_q[2]), .Q1(dip_7410_1_q1),
    .Q2(dip_7410_1_q2), .Q3(dip_7410_1_q3));
  nand nand_1 (nand_1_out, counter_1_q[0], counter_1_q[1], counter_1_q[2]);
  xnor xnor_1 (xnor_1_out, nand_1_out, dip_7410_1_q1);
  xnor xnor_2 (xnor_2_out, nand_1_out, dip_7410_1_q3);
  xnor xnor_3 (xnor_3_out, nand_1_out, dip_7410_1_q2);
  LED led_1 (.in(and_1_out));
  and and_1 (and_1_out, xnor_1_out, xnor_2_out, xnor_3_out);
endmodule

module Test_7411 (
);

  wire and_1_out, and_2_out, clock_1_out, dip_7411_1_q1, dip_7411_1_q2, dip_7411_1_q3, xnor_1_out,
       xnor_2_out, xnor_3_out;
  wire [2:0] counter_1_q;

  Clock clock_1 (.out(clock_1_out));
  Counter #(.width(3), .max('h7)) counter_1 (
    .count(1'b1), .Q(counter_1_q), .clk(clock_1_out));  // open: load, D, carry, clr
  DIP_7411 dip_7411_1 (
    .A1(counter_1_q[0]), .B1(counter_1_q[1]), .C1(counter_1_q[2]), .A2(counter_1_q[0]), .B2(counter_1_q[1]),
    .C2(counter_1_q[2]), .A3(counter_1_q[0]), .B3(counter_1_q[1]), .C3(counter_1_q[2]), .Q1(dip_7411_1_q1),
    .Q2(dip_7411_1_q2), .Q3(dip_7411_1_q3));
  and and_1 (and_1_out, counter_1_q[0], counter_1_q[1], counter_1_q[2]);
  xnor xnor_1 (xnor_1_out, and_1_out, dip_7411_1_q1);
  xnor xnor_2 (xnor_2_out, and_1_out, dip_7411_1_q3);
  xnor xnor_3 (xnor_3_out, and_1_out, dip_7411_1_q2);
  and and_2 (and_2_out, xnor_1_out, xnor_2_out, xnor_3_out);
  LED led_1 (.in(and_2_out));
endmodule

module Test_7420 (
);

  wire and_1_out, clock_1_out, dip_7420_1_q1, dip_7420_1_q2, nand_1_out, xnor_1_out, xnor_2_out;
  wire [3:0] counter_1_q;

  Clock clock_1 (.out(clock_1_out));
  Counter #(.width(4), .max('hf)) counter_1 (
    .count(1'b1), .Q(counter_1_q), .clk(clock_1_out));  // open: load, D, carry, clr
  DIP_7420 dip_7420_1 (
    .A1(counter_1_q[0]), .B1(counter_1_q[1]), .C1(counter_1_q[2]), .D1(counter_1_q[3]), .A2(counter_1_q[0]),
    .B2(counter_1_q[1]), .C2(counter_1_q[2]), .D2(counter_1_q[3]), .Q1(dip_7420_1_q1), .Q2(dip_7420_1_q2));
  nand nand_1 (nand_1_out, counter_1_q[0], counter_1_q[1], counter_1_q[2], counter_1_q[3]);
  xnor xnor_1 (xnor_1_out, nand_1_out, dip_7420_1_q2);
  xnor xnor_2 (xnor_2_out, nand_1_out, dip_7420_1_q1);
  LED led_1 (.in(and_1_out));
  and and_1 (and_1_out, xnor_1_out, xnor_2_out);
endmodule

module Test_7421 (
);

  wire and_1_out, and_2_out, clock_1_out, dip_7421_1_q1, dip_7421_1_q2, xnor_1_out, xnor_2_out;
  wire [3:0] counter_1_q;

  Clock clock_1 (.out(clock_1_out));
  Counter #(.width(4), .max('hf)) counter_1 (
    .count(1'b1), .Q(counter_1_q), .clk(clock_1_out));  // open: load, D, carry, clr
  DIP_7421 dip_7421_1 (
    .A1(counter_1_q[0]), .B1(counter_1_q[1]), .C1(counter_1_q[2]), .D1(counter_1_q[3]), .A2(counter_1_q[0]),
    .B2(counter_1_q[1]), .C2(counter_1_q[2]), .D2(counter_1_q[3]), .Q1(dip_7421_1_q1), .Q2(dip_7421_1_q2));
  and and_1 (and_1_out, counter_1_q[0], counter_1_q[1], counter_1_q[2], counter_1_q[3]);
  xnor xnor_1 (xnor_1_out, and_1_out, dip_7421_1_q2);
  xnor xnor_2 (xnor_2_out, and_1_out, dip_7421_1_q1);
  and and_2 (and_2_out, xnor_1_out, xnor_2_out);
  LED led_1 (.in(and_2_out));
endmodule

module Test_7425 (
);

  wire and_1_out, clock_1_out, dip_7425_1_q1, dip_7425_1_q2, nor_1_out, xnor_1_out, xnor_2_out;
  wire [3:0] counter_1_q;

  Clock clock_1 (.out(clock_1_out));
  Counter #(.width(4), .max('hf)) counter_1 (
    .count(1'b1), .Q(counter_1_q), .clk(clock_1_out));  // open: load, D, carry, clr
  DIP_7425 dip_7425_1 (
    .A1(counter_1_q[0]), .B1(counter_1_q[1]), .C1(counter_1_q[2]), .D1(counter_1_q[3]), .A2(counter_1_q[0]),
    .B2(counter_1_q[1]), .C2(counter_1_q[2]), .D2(counter_1_q[3]), .Q1(dip_7425_1_q1), .Q2(dip_7425_1_q2));
  nor nor_1 (nor_1_out, counter_1_q[0], counter_1_q[1], counter_1_q[2], counter_1_q[3]);
  xnor xnor_1 (xnor_1_out, nor_1_out, dip_7425_1_q2);
  xnor xnor_2 (xnor_2_out, nor_1_out, dip_7425_1_q1);
  LED led_1 (.in(and_1_out));
  and and_1 (and_1_out, xnor_1_out, xnor_2_out);
endmodule

module Test_7427 (
);

  wire and_1_out, clock_1_out, dip_7427_1_q1, dip_7427_1_q2, dip_7427_1_q3, nor_1_out, xnor_1_out,
       xnor_2_out, xnor_3_out;
  wire [2:0] counter_1_q;

  Clock clock_1 (.out(clock_1_out));
  Counter #(.width(3), .max('h7)) counter_1 (
    .count(1'b1), .Q(counter_1_q), .clk(clock_1_out));  // open: load, D, carry, clr
  DIP_7427 dip_7427_1 (
    .A1(counter_1_q[0]), .B1(counter_1_q[1]), .C1(counter_1_q[2]), .A2(counter_1_q[0]), .B2(counter_1_q[1]),
    .C2(counter_1_q[2]), .A3(counter_1_q[0]), .B3(counter_1_q[1]), .C3(counter_1_q[2]), .Q1(dip_7427_1_q1),
    .Q2(dip_7427_1_q2), .Q3(dip_7427_1_q3));
  nor nor_1 (nor_1_out, counter_1_q[0], counter_1_q[1], counter_1_q[2]);
  xnor xnor_1 (xnor_1_out, nor_1_out, dip_7427_1_q1);
  xnor xnor_2 (xnor_2_out, nor_1_out, dip_7427_1_q3);
  xnor xnor_3 (xnor_3_out, nor_1_out, dip_7427_1_q2);
  LED led_1 (.in(and_1_out));
  and and_1 (and_1_out, xnor_1_out, xnor_2_out, xnor_3_out);
endmodule

module Test_7432 (
);

  wire and_1_out, clock_1_out, dip_7432_1_q1, dip_7432_1_q2, dip_7432_1_q3, dip_7432_1_q4, or_1_out,
       xnor_1_out, xnor_2_out, xnor_3_out, xnor_4_out;
  wire [1:0] counter_1_q;

  Clock clock_1 (.out(clock_1_out));
  Counter #(.width(2), .max('h3)) counter_1 (
    .count(1'b1), .Q(counter_1_q), .clk(clock_1_out));  // open: load, D, carry, clr
  DIP_7432 dip_7432_1 (
    .A1(counter_1_q[0]), .B1(counter_1_q[1]), .A2(counter_1_q[0]), .B2(counter_1_q[1]), .A3(counter_1_q[0]),
    .B3(counter_1_q[1]), .A4(counter_1_q[0]), .B4(counter_1_q[1]), .Q1(dip_7432_1_q1), .Q2(dip_7432_1_q2),
    .Q3(dip_7432_1_q3), .Q4(dip_7432_1_q4));
  or or_1 (or_1_out, counter_1_q[0], counter_1_q[1]);
  xnor xnor_1 (xnor_1_out, or_1_out, dip_7432_1_q4);
  xnor xnor_2 (xnor_2_out, or_1_out, dip_7432_1_q3);
  xnor xnor_3 (xnor_3_out, or_1_out, dip_7432_1_q1);
  xnor xnor_4 (xnor_4_out, or_1_out, dip_7432_1_q2);
  LED led_1 (.in(and_1_out));
  and and_1 (and_1_out, xnor_1_out, xnor_2_out, xnor_3_out, xnor_4_out);
endmodule

module Test_4786 (
);

  wire and_1_out, clock_1_out, dip_7486_1_q1, dip_7486_1_q2, dip_7486_1_q3, dip_7486_1_q4, xnor_1_out,
       xnor_2_out, xnor_3_out, xnor_4_out, xor_1_out;
  wire [1:0] counter_1_q;

  Clock clock_1 (.out(clock_1_out));
  Counter #(.width(2), .max('h3)) counter_1 (
    .count(1'b1), .Q(counter_1_q), .clk(clock_1_out));  // open: load, D, carry, clr
  DIP_7486 dip_7486_1 (
    .A1(counter_1_q[0]), .B1(counter_1_q[1]), .A2(counter_1_q[0]), .B2(counter_1_q[1]), .A3(counter_1_q[0]),
    .B3(counter_1_q[1]), .A4(counter_1_q[0]), .B4(counter_1_q[1]), .Q1(dip_7486_1_q1), .Q2(dip_7486_1_q2),
    .Q3(dip_7486_1_q3), .Q4(dip_7486_1_q4));
  xor xor_1 (xor_1_out, counter_1_q[0], counter_1_q[1]);
  xnor xnor_1 (xnor_1_out, xor_1_out, dip_7486_1_q4);
  xnor xnor_2 (xnor_2_out, xor_1_out, dip_7486_1_q3);
  xnor xnor_3 (xnor_3_out, xor_1_out, dip_7486_1_q1);
  xnor xnor_4 (xnor_4_out, xor_1_out, dip_7486_1_q2);
  LED led_1 (.in(and_1_out));
  and and_1 (and_1_out, xnor_1_out, xnor_2_out, xnor_3_out, xnor_4_out);
endmodule

module Test_74147 (
);

  wire and_1_out, clock_1_out, not_1_out, not_2_out, not_3_out, not_4_out, not_5_out, not_6_out, not_7_out,
       not_8_out, not_9_out, not_10_out, not_11_out, not_12_out, not_13_out, not_14_out, undriven,
       undriven_2, undriven_3, undriven_4, xnor_1_out, xnor_2_out, xnor_3_out, xnor_4_out;
  wire [3:0] counter_1_q, priority_encoder_1_out;
  wire [9:0] shifter_1_out;

  Clock clock_1 (.out(clock_1_out));
  Shifter #(.width(10), .shift("rl")) shifter_1 (.in(10'h1ff), .\dist (counter_1_q), .out(shifter_1_out));
  Counter #(.width(4), .max('hf)) counter_1 (
    .count(1'b1), .Q(counter_1_q), .clk(clock_1_out));  // open: load, D, carry, clr
  not not_1 (not_1_out, shifter_1_out[9]);
  not not_2 (not_2_out, shifter_1_out[0]);
  not not_3 (not_3_out, shifter_1_out[1]);
  not not_4 (not_4_out, shifter_1_out[2]);
  not not_5 (not_5_out, shifter_1_out[3]);
  not not_6 (not_6_out, shifter_1_out[4]);
  not not_7 (not_7_out, shifter_1_out[5]);
  not not_8 (not_8_out, shifter_1_out[6]);
  not not_9 (not_9_out, shifter_1_out[7]);
  not not_10 (not_10_out, shifter_1_out[8]);
  Priority_Encoder #(.select(4)) priority_encoder_1 (
    .in0(not_1_out), .in1(not_2_out), .in2(not_3_out), .in3(not_4_out), .in4(not_5_out), .in5(not_6_out),
    .in6(not_7_out), .in7(not_8_out), .in8(not_9_out), .in9(not_10_out), .out(priority_encoder_1_out));  // open: in10, in11, in12, in13, in14, in15, gs, en_out, en_in
  not not_11 (not_11_out, priority_encoder_1_out[1]);
  not not_12 (not_12_out, priority_encoder_1_out[2]);
  not not_13 (not_13_out, priority_encoder_1_out[3]);
  not not_14 (not_14_out, priority_encoder_1_out[0]);
  xnor xnor_1 (xnor_1_out, undriven_4, not_14_out);
  xnor xnor_2 (xnor_2_out, undriven_2, not_11_out);
  xnor xnor_3 (xnor_3_out, undriven, not_12_out);
  xnor xnor_4 (xnor_4_out, undriven_3, not_13_out);
  and and_1 (and_1_out, xnor_1_out, xnor_2_out, xnor_3_out, xnor_4_out);
  LED led_1 (.in(and_1_out));
endmodule

module Test_74283 (
);

  wire adder_1_cout, and_1_out, clock_1_out, dip_74283_1_cout, dip_74283_1_q1, dip_74283_1_q2,
       dip_74283_1_q3, dip_74283_1_q4, xnor_1_out, xnor_2_out, xnor_3_out, xnor_4_out, xnor_5_out;
  wire [3:0] adder_1_out, counter_1_q, counter_1_q_2;
  wire [8:8] counter_1_q_3;

  Clock clock_1 (.out(clock_1_out));
  Counter #(.width(9), .max('h1ff)) counter_1 (
    .count(1'b1), .Q({counter_1_q_3[8], counter_1_q_2, counter_1_q}), .clk(clock_1_out));  // open: load, D, carry, clr
  Adder #(.width(4)) adder_1 (
    .a(counter_1_q), .b(counter_1_q_2), .out(adder_1_out), .cin(counter_1_q_3[8]), .cout(adder_1_cout));
  DIP_74283 dip_74283_1 (
    .CIN(counter_1_q_3[8]), .A1(counter_1_q[0]), .B1(counter_1_q_2[0]), .A2(counter_1_q[1]),
    .B2(counter_1_q_2[1]), .A3(counter_1_q[2]), .B3(counter_1_q_2[2]), .A4(counter_1_q[3]),
    .B4(counter_1_q_2[3]), .Q1(dip_74283_1_q1), .Q2(dip_74283_1_q2), .Q3(dip_74283_1_q3),
    .Q4(dip_74283_1_q4), .COUT(dip_74283_1_cout));
  xnor xnor_1 (xnor_1_out, dip_74283_1_q1, adder_1_out[0]);
  xnor xnor_2 (xnor_2_out, dip_74283_1_q2, adder_1_out[1]);
  xnor xnor_3 (xnor_3_out, dip_74283_1_q3, adder_1_out[2]);
  xnor xnor_4 (xnor_4_out, dip_74283_1_q4, adder_1_out[3]);
  xnor xnor_5 (xnor_5_out, dip_74283_1_cout, adder_1_cout);
  and and_1 (and_1_out, xnor_1_out, xnor_2_out, xnor_3_out, xnor_4_out, xnor_5_out);
  LED led_1 (.in(and_1_out));
endmodule

module Test_744075 (
);

  wire and_1_out, clock_1_out, dip_744075_1_q1, dip_744075_1_q2, dip_744075_1_q3, or_1_out, xnor_1_out,
       xnor_2_out, xnor_3_out;
  wire [2:0] counter_1_q;

  Clock clock_1 (.out(clock_1_out));
  Counter #(.width(3), .max('h7)) counter_1 (
    .count(1'b1), .Q(counter_1_q), .clk(clock_1_out));  // open: load, D, carry, clr
  DIP_744075 dip_744075_1 (
    .A1(counter_1_q[0]), .B1(counter_1_q[1]), .C1(counter_1_q[2]), .A2(counter_1_q[0]), .B2(counter_1_q[1]),
    .C2(counter_1_q[2]), .A3(counter_1_q[0]), .B3(counter_1_q[1]), .C3(counter_1_q[2]), .Q1(dip_744075_1_q1),
    .Q2(dip_744075_1_q2), .Q3(dip_744075_1_q3));
  or or_1 (or_1_out, counter_1_q[0], counter_1_q[1], counter_1_q[2]);
  xnor xnor_1 (xnor_1_out, or_1_out, dip_744075_1_q3);
  xnor xnor_2 (xnor_2_out, or_1_out, dip_744075_1_q2);
  xnor xnor_3 (xnor_3_out, or_1_out, dip_744075_1_q1);
  LED led_1 (.in(and_1_out));
  and and_1 (and_1_out, xnor_1_out, xnor_2_out, xnor_3_out);
endmodule

module Test_744511 (
  input  LE,
  input  LT_,
  input  BL_
);

  wire clock_1_out, dip_744511_1_qa, dip_744511_1_qb, dip_744511_1_qc, dip_744511_1_qd, dip_744511_1_qe,
       dip_744511_1_qf, dip_744511_1_qg;
  wire [3:0] counter_1_q;

  Clock clock_1 (.out(clock_1_out));
  Counter #(.width(4), .max('hf)) counter_1 (
    .count(1'b1), .Q(counter_1_q), .clk(clock_1_out));  // open: load, D, carry, clr
  DIP_744511 dip_744511_1 (
    .LT_(LT_), .D1(counter_1_q[0]), .D2(counter_1_q[1]), .D3(counter_1_q[2]), .D4(counter_1_q[3]), .LE(LE),
    .BL_(BL_), .Qa(dip_744511_1_qa), .Qb(dip_744511_1_qb), .Qc(dip_744511_1_qc), .Qd(dip_744511_1_qd),
    .Qe(dip_744511_1_qe), .Qf(dip_744511_1_qf), .Qg(dip_744511_1_qg));
  _7_Segment_Display u_7_segment_display_1 (
    .g(dip_744511_1_qg), .f(dip_744511_1_qf), .a(dip_744511_1_qa), .b(dip_744511_1_qb), .e(dip_744511_1_qe),
    .d(dip_744511_1_qd), .c(dip_744511_1_qc));  // open: dp
endmodule
